// Digital circuit tarea1_Marianela_Arcila.dig as structural Verilog
module tarea1_Marianela_Arcila (
  input  E0,
  input  S0,
  input  S1,
  input  S2,
  input  E1,
  input  E2,
  input  E3,
  input  E4,
  input  E5,
  input  E6,
  input  E7,
  input  E0_2,
  input  S0_2,
  input  S1_2
);

  wire and_1_out, and_2_out, and_3_out, and_4_out, and_5_out, and_6_out, and_7_out, and_8_out, and_9_out,
       and_10_out, and_11_out, and_12_out, and_13_out, and_14_out, not_1_out, not_2_out, not_3_out,
       not_4_out, not_5_out, or_1_out, or_2_out, or_3_out;

  not not_1 (not_1_out, S0);
  not not_2 (not_2_out, S1);
  not not_3 (not_3_out, S2);
  and and_1 (and_1_out, E0, not_1_out, not_2_out, not_3_out);
  and and_2 (and_2_out, E1, S0, not_3_out, not_2_out);
  and and_3 (and_3_out, E2, not_1_out, S1, not_3_out);
  and and_4 (and_4_out, E3, S0, S1, not_3_out);
  and and_5 (and_5_out, E4, not_1_out, not_2_out, S2);
  and and_6 (and_6_out, E5, S0, not_2_out, S2);
  and and_7 (and_7_out, E6, S0, S1, not_3_out);
  and and_8 (and_8_out, E7, S0, S1, S2);
  or or_1 (or_1_out, and_1_out, and_2_out, and_3_out, and_4_out);
  or or_2 (or_2_out, and_5_out, and_6_out, and_7_out, and_8_out);
  and and_9 (and_9_out, or_1_out, or_1_out);
  and and_10 (and_10_out, or_2_out, or_2_out);
  or or_3 (or_3_out, and_9_out, and_10_out);
  LED Salida (.in(or_3_out));
  not not_4 (not_4_out, S0_2);
  not not_5 (not_5_out, S1_2);
  and and_11 (and_11_out, E0_2, not_4_out, not_5_out);
  and and_12 (and_12_out, E0_2, not_4_out, S1_2);
  and and_13 (and_13_out, E0_2, S0_2, not_5_out);
  and and_14 (and_14_out, E0_2, S0_2, S1_2);
  LED Y0 (.in(and_11_out));
  LED Y1 (.in(and_12_out));
  LED Y2 (.in(and_13_out));
  LED Y3 (.in(and_14_out));

  // Notes on the sheet:
  //   Para crear el multiplexor de 8 entradas y una salida, se utilizaron dos multiplexores de 
  //   4 entradas, los cuales estan conectados a dos compuertas logicas AND que a su vez
  //   van unidas por una compuerta OR hacia la salida (una especie de multiplexor de dos entradas 1 salida),
  //   esto para poder relacionar los dos multiplexores a una salida unica
  //   Multiplexor de 8 Entradas 1 Salida
  //   En Demultiplexor tiene una entrada, la cual es trasmitida a una de las 4 salidas
  //   segun el tipo de combinacion de activacion  se se ecoja en los S0 y S1, este sistema
  //   tiene compuertas AND y para negar los valores de S se utilizan compuertas NOT
  //   Demultiplexor de 1 Entrada 4 Salidas
endmodule
